# Fritzing sketch Fritzing Schaltung 1 (saved by Fritzing 0.9.3b)
breadboards: 1

parts:
  Bauteil1 = Arduino Uno (Rev3)
  R1 = Resistor [tolerance=±5% resistance=100 package="2512 [SMD]"]
  R2 = Resistor [tolerance=±5% resistance=100 package=THT]
  LED2 = LED - 5mm [color="Yellow (595nm)" package="5 mm [THT]"]
  LED3 = LED - 5mm [color="White (4500K)" package="5 mm [THT]"]
  R3 = Resistor [tolerance=±5% resistance=100 package=THT]
  R4 = Resistor [tolerance=±5% resistance=100 package=THT]
  LED4 = LED - 5mm [color="White (4500K)" package="5 mm [THT]"]
  LED5 = LED - 5mm [color="Red (633nm)" package="5 mm [THT]"]
  R5 = Resistor [tolerance=±5% resistance=100 package=THT]
  R6 = Resistor [tolerance=±5% resistance=100 package=THT]
  LED6 = LED - 5mm [color="Yellow (595nm)" package="5 mm [THT]"]
  LED7 = LED - 5mm [color="Red (633nm)" package="5 mm [THT]"]
  S1 = Pushbutton [package="[THT]"]
  R7 = Resistor [tolerance=±5% resistance=10k package=THT]

nets:
  N1: Bauteil1.D8, S1.Pin_1, S1.Pin_2, R7.Pin_0
  N2: Bauteil1.D2, R1.Pin_0
  N3: Bauteil1.D3_PWM, R2.Pin_0
  N4: Bauteil1.D4, R3.Pin_0
  N5: Bauteil1.D5_PWM, R4.Pin_0
  N6: Bauteil1.D6_PWM, R6.Pin_0
  N7: Bauteil1.D7, R5.Pin_0
  N8: Bauteil1.5V, S1.Pin_3, S1.Pin_4
  N9: Bauteil1.GND, LED2.anode, LED3.anode, LED4.anode, LED5.anode, LED6.anode, LED7.anode, R7.Pin_1
  N10: R1.Pin_1, LED3.cathode
  N11: R2.Pin_1, LED2.cathode
  N12: R3.Pin_1, LED5.cathode
  N13: R4.Pin_1, LED4.cathode
  N14: R5.Pin_1, LED7.cathode
  N15: R6.Pin_1, LED6.cathode
