# Fritzing sketch Fritzing Schaltung 2 (saved by Fritzing 0.9.3b)
breadboards: 2

parts:
  Bauteil2 = Arduino Uno (Rev3)
  S2 = Pushbutton [package="[THT]"]
  R1 = Resistor [tolerance=±5% resistance=10k package=THT]
  R2 = Resistor [tolerance=±5% resistance=10k package=THT]
  S3 = Pushbutton [package="[THT]"]
  LED1 = LED - 5mm [color="White (6500K)" package="5 mm [THT]"]
  R3 = Resistor [tolerance=±5% resistance=100 package=THT]
  R4 = Resistor [tolerance=±5% resistance=100 package=THT]
  LED2 = LED - 5mm [color="Green (555nm)" package="5 mm [THT]"]
  R5 = Resistor [tolerance=±5% resistance=100 package=THT]
  LED3 = LED - 5mm [color="Green (555nm)" package="5 mm [THT]"]

nets:
  N1: Bauteil2.D11_PWM/MOSI, LED1.cathode
  N2: Bauteil2.D12/MISO, R4.Pin_0
  N3: Bauteil2.D13/SCK, R5.Pin_1
  N4: Bauteil2.D2, S2.Pin_3, S2.Pin_4, R1.Pin_1
  N5: Bauteil2.D3_PWM, R2.Pin_1, S3.Pin_3, S3.Pin_4
  N6: Bauteil2.5V, S2.Pin_1, S2.Pin_2, S3.Pin_1, S3.Pin_2
  N7: Bauteil2.GND, R1.Pin_0, R2.Pin_0, R3.Pin_0, LED2.anode, LED3.cathode
  N8: LED1.anode, R3.Pin_1
  N9: R4.Pin_1, LED2.cathode
  N10: R5.Pin_0, LED3.anode
